// Logisim project Processor.circ as structural Verilog: 8 circuits, main circuit main
module main (
  input  [1:0] MC
);

  wire Clock_out;
  wire [7:0] instructions_fetch_1_pc_1;
  wire [31:0] instructions_fetch_1_inst;

  Clock Clock (.out(Clock_out));
  Instructions_Fetch instructions_fetch_1 (
    .Mc(MC), .Clock(Clock_out), .PC_1(instructions_fetch_1_pc_1), .Inst(instructions_fetch_1_inst));
  IF_ID if_id_1 (
    .Clock(Clock_out), .Inst_in(instructions_fetch_1_inst), .PC_1_in(instructions_fetch_1_pc_1));  // open: Inst_out, PC_1_out
endmodule

// Register
module Register_File (
  input  [31:0] D_12,
  input  [4:0] Rw,
  input  W,
  input  [4:0] Ra,
  input  [4:0] Rb,
  output [31:0] Qa,
  output [31:0] Qb
);

  wire and_1_out, and_2_out, and_3_out, and_4_out, and_5_out, and_6_out, and_7_out, and_9_out, and_10_out,
       and_11_out, and_12_out, and_13_out, and_14_out, and_15_out, and_16_out, and_17_out, and_19_out,
       and_20_out, and_21_out, and_22_out, and_23_out, and_25_out, and_26_out, and_27_out, and_28_out,
       and_29_out, and_30_out, clock_1_out, decoder_1_out1, decoder_1_out2, decoder_1_out3, decoder_1_out4,
       decoder_1_out5, decoder_1_out6, decoder_1_out7, decoder_1_out8, decoder_1_out9, decoder_1_out10,
       decoder_1_out11, decoder_1_out12, decoder_1_out13, decoder_1_out14, decoder_1_out15, decoder_1_out16,
       decoder_1_out17, decoder_1_out18, decoder_1_out19, decoder_1_out20, decoder_1_out21, decoder_1_out22,
       decoder_1_out23, decoder_1_out25, decoder_1_out26, decoder_1_out27, decoder_1_out28, decoder_1_out29,
       decoder_1_out30, decoder_1_out31, undriven;
  wire [31:0] _0_q, _1_q, _2_q, _3_q, _4_q, _5_q, _6_q, _7_q, _8_q, _9_q, _10_q, _11_q, _12_q, _13_q, _14_q,
       _15_q, _16_q, _17_q, _19_q, _20_q, _21_q, _22_q, _23_q, _24_q, _25_q, _26_q, _27_q, _28_2_q, _28_q,
       _29_q, _31_q, undriven_2;

  Decoder #(.select(5), .enable("false")) decoder_1 (
    .out1(decoder_1_out1), .out2(decoder_1_out2), .out3(decoder_1_out3), .out4(decoder_1_out4),
    .out5(decoder_1_out5), .out6(decoder_1_out6), .out7(decoder_1_out7), .out8(decoder_1_out8),
    .out9(decoder_1_out9), .out10(decoder_1_out10), .out11(decoder_1_out11), .out12(decoder_1_out12),
    .out13(decoder_1_out13), .out14(decoder_1_out14), .out15(decoder_1_out15), .out16(decoder_1_out16),
    .out17(decoder_1_out17), .out18(decoder_1_out18), .out19(decoder_1_out19), .out20(decoder_1_out20),
    .out21(decoder_1_out21), .out22(decoder_1_out22), .out23(decoder_1_out23), .out24(W),
    .out25(decoder_1_out25), .out26(decoder_1_out26), .out27(decoder_1_out27), .out28(decoder_1_out28),
    .out29(decoder_1_out29), .out30(decoder_1_out30), .out31(decoder_1_out31), .sel(Rw));  // open: out0
  Clock clock_1 (.out(clock_1_out));
  and and_1 (and_1_out, W, decoder_1_out1);
  and and_2 (and_2_out, W, decoder_1_out2);
  and and_3 (and_3_out, W, decoder_1_out3);
  and and_4 (and_4_out, W, decoder_1_out4);
  and and_5 (and_5_out, W, decoder_1_out5);
  and and_6 (and_6_out, W, decoder_1_out6);
  and and_7 (and_7_out, W, decoder_1_out7);
  and and_8 (and_7_out, W, decoder_1_out7);
  Register #(.width(32)) _0 (.Q(_0_q));  // open: D, en, clk, clr
  Register #(.width(32)) _1 (.D(D_12), .en(and_1_out), .Q(_1_q), .clk(clock_1_out));  // open: clr
  Register #(.width(32)) _2 (.D(D_12), .en(and_2_out), .Q(_2_q), .clk(clock_1_out));  // open: clr
  Register #(.width(32)) _3 (.D(D_12), .en(and_3_out), .Q(_3_q), .clk(clock_1_out));  // open: clr
  Register #(.width(32)) _4 (.D(D_12), .en(and_4_out), .Q(_4_q), .clk(clock_1_out));  // open: clr
  Register #(.width(32)) _5 (.D(D_12), .en(and_5_out), .Q(_5_q), .clk(clock_1_out));  // open: clr
  Register #(.width(32)) _6 (.D(D_12), .en(and_6_out), .Q(_6_q), .clk(clock_1_out));  // open: clr
  Register #(.width(32)) _7 (.D(D_12), .en(and_7_out), .Q(_7_q), .clk(clock_1_out));  // open: clr
  and and_9 (and_9_out, W, decoder_1_out8);
  and and_10 (and_10_out, W, decoder_1_out9);
  and and_11 (and_11_out, W, decoder_1_out10);
  and and_12 (and_12_out, W, decoder_1_out11);
  and and_13 (and_13_out, W, decoder_1_out13);
  and and_14 (and_14_out, W, decoder_1_out14);
  and and_15 (and_15_out, W, decoder_1_out15);
  Register #(.width(32)) _8 (.D(D_12), .en(and_9_out), .Q(_8_q), .clk(clock_1_out));  // open: clr
  Register #(.width(32)) _9 (.D(D_12), .en(and_10_out), .Q(_9_q), .clk(clock_1_out));  // open: clr
  Register #(.width(32)) _10 (.D(D_12), .en(and_11_out), .Q(_10_q), .clk(clock_1_out));  // open: clr
  Register #(.width(32)) _11 (.D(D_12), .en(and_12_out), .Q(_11_q), .clk(clock_1_out));  // open: clr
  Register #(.width(32)) _12 (.D(D_12), .Q(_12_q), .clk(clock_1_out));  // open: en, clr
  Register #(.width(32)) _13 (.D(D_12), .en(and_13_out), .Q(_13_q), .clk(clock_1_out));  // open: clr
  Register #(.width(32)) _14 (.D(D_12), .en(and_14_out), .Q(_14_q), .clk(clock_1_out), .clr(undriven));
  Register #(.width(32)) _14_2 (.D(D_12), .en(and_14_out), .Q(_14_q), .clk(clock_1_out), .clr(undriven));
  Register #(.width(32)) _15 (.D(D_12), .en(and_15_out), .Q(_15_q), .clk(clock_1_out));  // open: clr
  and and_16 (and_16_out, W, decoder_1_out16);
  and and_17 (and_17_out, W, decoder_1_out17);
  and and_18 (and_17_out, W, decoder_1_out17);
  and and_19 (and_19_out, W, decoder_1_out18);
  and and_20 (and_20_out, W, decoder_1_out19);
  and and_21 (and_21_out, W, decoder_1_out20);
  and and_22 (and_22_out, W, decoder_1_out21);
  and and_23 (and_23_out, W, decoder_1_out22);
  and and_24 (and_23_out, W, decoder_1_out22);
  and and_25 (and_25_out, W, decoder_1_out23);
  Register #(.width(32)) _16 (.D(D_12), .en(and_16_out), .Q(_16_q), .clk(clock_1_out));  // open: clr
  Register #(.width(32)) _17 (.D(D_12), .en(and_17_out), .Q(_17_q), .clk(clock_1_out));  // open: clr
  Register #(.width(32)) _28 (.D(D_12), .en(and_19_out), .Q(_28_q), .clk(clock_1_out));  // open: clr
  Register #(.width(32)) _19 (.D(D_12), .en(and_20_out), .Q(_19_q), .clk(clock_1_out));  // open: clr
  Register #(.width(32)) _20 (.D(D_12), .en(and_21_out), .Q(_20_q), .clk(clock_1_out));  // open: clr
  Register #(.width(32)) _21 (.D(D_12), .en(and_22_out), .Q(_21_q), .clk(clock_1_out));  // open: clr
  Register #(.width(32)) _22 (.D(D_12), .en(and_23_out), .Q(_22_q), .clk(clock_1_out));  // open: clr
  Register #(.width(32)) _23 (.D(D_12), .en(and_25_out), .Q(_23_q), .clk(clock_1_out));  // open: clr
  and and_26 (and_26_out, W, W);
  and and_27 (and_27_out, W, decoder_1_out25);
  and and_28 (and_28_out, W, decoder_1_out26);
  and and_29 (and_29_out, W, decoder_1_out27);
  and and_30 (and_30_out, W, decoder_1_out28);
  // AND_Gate and_31 has open pins: in0=W, in1=decoder_1_out31, out=open
  Register #(.width(32)) _24 (.D(D_12), .en(and_26_out), .Q(_24_q), .clk(clock_1_out));  // open: clr
  Register #(.width(32)) _25 (.D(D_12), .en(and_27_out), .Q(_25_q), .clk(clock_1_out));  // open: clr
  Register #(.width(32)) _26 (.D(D_12), .en(and_28_out), .Q(_26_q), .clk(clock_1_out));  // open: clr
  Register #(.width(32)) _27 (.D(D_12), .en(and_29_out), .Q(_27_q), .clk(clock_1_out));  // open: clr
  Register #(.width(32)) _28_2 (.D(D_12), .en(and_30_out), .Q(_28_2_q), .clk(clock_1_out));  // open: clr
  Register #(.width(32)) _29 (.D(D_12), .Q(_29_q), .clk(clock_1_out));  // open: en, clr
  Register #(.width(32)) _31 (.D(D_12), .Q(_31_q), .clk(clock_1_out));  // open: en, clr
  Multiplexer #(.select(5), .width(32), .enable("false")) multiplexer_1 (
    .in0(_0_q), .in1(_1_q), .in2(_2_q), .in3(_3_q), .in4(_4_q), .in5(_5_q), .in6(_6_q), .in7(_7_q),
    .in8(_8_q), .in9(_9_q), .in10(_10_q), .in11(_11_q), .in12(_12_q), .in13(_13_q), .in14(_14_q),
    .in15(_15_q), .in16(_16_q), .in17(_17_q), .in18(_28_q), .in19(_19_q), .in20(_20_q), .in21(_21_q),
    .in22(_22_q), .in23(_23_q), .in24(_24_q), .in25(_25_q), .in26(_26_q), .in27(_27_q), .in28(_28_2_q),
    .in29(_29_q), .in30(_31_q), .in31(undriven_2), .out(Qa), .sel(Ra));
  Multiplexer #(.select(5), .width(32), .enable("false")) multiplexer_2 (
    .in0(_0_q), .in1(_1_q), .in2(_2_q), .in3(_3_q), .in4(_4_q), .in5(_5_q), .in6(_6_q), .in7(_7_q),
    .in8(_8_q), .in9(_9_q), .in10(_10_q), .in11(_11_q), .in12(_12_q), .in13(_13_q), .in14(_14_q),
    .in15(_15_q), .in16(_16_q), .in17(_17_q), .in18(_28_q), .in19(_19_q), .in20(_20_q), .in21(_21_q),
    .in22(_22_q), .in23(_23_q), .in24(_24_q), .in25(_25_q), .in26(_26_q), .in27(_27_q), .in28(_28_2_q),
    .in29(_29_q), .in30(_31_q), .in31(undriven_2), .out(Qb), .sel(Rb));
endmodule

module Instructions_Fetch (
  input  [1:0] Mc,
  input  Clock,
  output [7:0] PC_1,
  output [31:0] Inst
);

  wire and_1_out;
  wire [1:0] not_1_out;
  wire [7:0] register_1_q;

  Adder adder_1 (.a(register_1_q), .b(8'h1), .out(PC_1));  // open: cin, cout
  Register register_1 (.D(PC_1), .Q(register_1_q), .clk(Clock));  // open: en, clr
  ROM #(.dataWidth(32)) rom_1 (.addr(register_1_q), .data(Inst), .sel(and_1_out));
  assign not_1_out = ~Mc;  // NOT_Gate not_1, 2 bits wide
  and and_1 (and_1_out, not_1_out[0], not_1_out[1]);
endmodule

module Decode (
  input  [31:0] Inst,
  input  [7:0] PC_4,
  input  [31:0] in_3,
  output [7:0] PC_4_2
);

  wire ltype_1_p2, ltype_1_p4, ltype_1_p5, multiplexer_1_out, rtype_1_p2, rtype_1_p3, typedetermine_1_output;

  // RType rtype_1: pin names not known; wires that end beside it: in_3, rtype_1_p2, rtype_1_p3
  // LType ltype_1: pin names not known; wires that end beside it: in_3, ltype_1_p2, rtype_1_p3, ltype_1_p4, ltype_1_p5
  TypeDetermine typedetermine_1 (.in_1(in_3), .Output(typedetermine_1_output));
  Multiplexer #(.enable("false")) multiplexer_1 (
    .in0(rtype_1_p2), .in1(ltype_1_p2), .out(multiplexer_1_out), .sel(typedetermine_1_output));
  Multiplexer #(.enable("false")) multiplexer_2 (.in1(ltype_1_p5), .sel(typedetermine_1_output));  // open: in0, out
  Register_File register_file_1 ();  // open: Qa, Qb, D_12, Rw, W, Ra, Rb

  assign PC_4_2 = PC_4;
endmodule

module IF_ID (
  input  Clock,
  input  [31:0] Inst_in,
  input  [7:0] PC_1_in,
  output [31:0] Inst_out,
  output [7:0] PC_1_out
);

  Register #(.width(32)) register_1 (.D(Inst_in), .Q(Inst_out), .clk(Clock));  // open: en, clr
  Register register_2 (.D(PC_1_in), .Q(PC_1_out), .clk(Clock));  // open: en, clr
endmodule

module RType (
  input  [31:0] Func,
  output [3:0] Opcode,
  output [4:0] Rs,
  output [4:0] Rt
);

  Multiplexer #(.select(5), .width(4), .enable("false")) multiplexer_1 (
    .in0(4'b0000), .in1(4'b0000), .in2(4'b0100), .in3(4'b0101), .in4(4'b0000), .in5(4'b0000), .in6(4'b0000),
    .in7(4'b0000), .in8(4'b0000), .in9(4'b0000), .in10(4'b0000), .in11(4'b0000), .in12(4'b0000),
    .in13(4'b0000), .in14(4'b0000), .in15(4'b0000), .in16(4'b0010), .in17(4'b0010), .in18(4'b0110),
    .in19(4'b0110), .in20(4'b1000), .in21(4'b1010), .in22(4'b1100), .in23(4'b1110), .in24(4'b0000),
    .in25(4'b0000), .in26(4'b1111), .in27(4'b1111), .in28(4'b0000), .in29(4'b0000), .in30(4'b0000),
    .in31(4'b0000), .out(Opcode), .sel({Func[5], Func[3:0]}));
  // Pins of 5 and 6 bits meet at Func[31:26]
  // Pins of 5 and 6 bits meet at Func[25:20]

  assign Rs = Func[24:20];
  assign Rt = Func[30:26];
endmodule

module TypeDetermine (
  input  [31:0] in_1,
  output Output
);

  wire [31:0] not_1_out;

  assign not_1_out = ~in_1;  // NOT_Gate not_1, 32 bits wide
  and and_1 (Output, not_1_out[26], not_1_out[27], not_1_out[28], not_1_out[29], not_1_out[30], not_1_out[31]);

  // Notes on the sheet:
  //   Output is on if type is register
endmodule

module LType (
  input  [31:0] Func,
  output [4:0] Src,
  output [4:0] Dest,
  output [15:0] Immidiate,
  output [3:0] Op
);

  Multiplexer #(.select(3), .width(4), .enable("false")) multiplexer_1 (
    .in0(4'b0000), .in1(4'b0010), .in2(4'b1111), .in3(4'b1111), .in4(4'b1000), .in5(4'b1010), .in6(4'b1100),
    .in7(4'b0000), .out(Op), .sel(Func[29:27]));

  assign Dest = Func[20:16];
  assign Immidiate = Func[15:0];
  assign Src = Func[25:21];
endmodule
