// Logisim project execute.circ as structural Verilog: 1 circuit, main circuit main
module main (
  input  [31:0] A,
  input  [31:0] B,
  input  [31:0] Imm,
  input  [7:0] PC
);

  wire [31:0] multiplexer_1_out;

  Multiplexer #(.width(32), .enable("false")) multiplexer_1 (.in0(B), .in1(Imm), .out(multiplexer_1_out));  // open: sel
  ALU_main ALU (.A(A), .B(multiplexer_1_out));  // open: Op, Sa, C, V
endmodule
